// Digital circuit four_bit_mux.dig as structural Verilog
module four_bit_mux (
  input  [3:0] a,
  input  [3:0] b,
  input  sel,
  output [3:0] y
);

  two_bit_mux two_bit_mux_1 (.a(a[3]), .b(b[3]), .s(sel), .y(y[3]));
  two_bit_mux two_bit_mux_2 (.a(a[2]), .b(b[2]), .s(sel), .y(y[2]));
  two_bit_mux two_bit_mux_3 (.a(a[1]), .b(b[1]), .s(sel), .y(y[1]));
  two_bit_mux two_bit_mux_4 (.a(a[0]), .b(b[0]), .s(sel), .y(y[0]));
endmodule
